# Fritzing sketch ESP8266 (saved by Fritzing 0.9.2b)
breadboards: 1

parts:
  R1 = Resistor [tolerance=±5% resistance=220 package=THT]
  LED1 = LED - 5mm [color="Red (633nm)" package="5 mm [THT]"]  # not connected
  Part1 = Arduino Uno (Rev3)
  R2 = Resistor [tolerance=±5% resistance=10k package=THT]
  U1 = ESP8266 WiFi Module [part_number=ESP8266]

nets:
  N1: R1.Pin_1, Part1.D5_PWM
  N2: Part1.D3_PWM, U1.TXD
  N3: Part1.D4, U1.RST
  N4: Part1.3V3, R2.Pin_0
  GND: Part1.GND, U1.GND
  N5: R2.Pin_1, U1.CH_PD

custom parts:
  ESP8266 WiFi Module: Generic WiFi Module based on the ESP8266 with onboard PCB antenna and UART communications
